# Fritzing sketch main (saved by Fritzing 0.9.4)
breadboards: 1

parts:
  Mod1 = Raspberry Pi Pico
  OLED1 = OLED-128x64-I2C-Monochrome-Display-GND-VDD_1

nets:
  N1: Mod1.pin_21, OLED1.connector3
  N2: Mod1.pin_22, OLED1.connector2
  N3: Mod1.pin_36, OLED1.connector1
  N4: Mod1.pin_38, OLED1.connector0

custom parts:
  Raspberry Pi Pico: Raspberry Pi Pico. Based around the RP2040 microcontroller the Pico is a low cost microcontroller device bringing Raspberry Pi quality, cost, and easy of use to the microcontroller space. Jan 2021, Split part in to two versions: tht (this one) and SMD. This one will drill holes for a .1 in header in pcb to allow plugging in the module as well as providing pads to solder the module to the top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
