# Fritzing sketch main (saved by Fritzing 0.9.4)
breadboards: 1

parts:
  DHT11_1 = DHT11 module
  Mod1 = Raspberry Pi Pico
  OLED1 = OLED 128x64 I2C Monochrome Display GND-VDD

nets:
  VCC: DHT11_1.VCC, Mod1.pin_36, OLED1.VDD
  GND: DHT11_1.GND, Mod1.pin_38, OLED1.GND
  N1: DHT11_1.DATA, Mod1.pin_24
  N2: Mod1.pin_21, OLED1.SDA
  N3: Mod1.pin_22, OLED1.SCK

custom parts:
  DHT11 module: https://cdn-learn.adafruit.com/downloads/pdf/dht.pdf DHT11 black pcb module reference by:https://github.com/adafruit/Fritzing-Library/blob/master/parts/DHT11%20Humitidy%20and%20Temperature%20Sensor.fzpz
  Raspberry Pi Pico: Raspberry Pi Pico. Based around the RP2040 microcontroller the Pico is a low cost microcontroller device bringing Raspberry Pi quality, cost, and easy of use to the microcontroller space. Jan 2021, Split part in to two versions: tht (this one) and SMD. This one will drill holes for a .1 in header in pcb to allow plugging in the module as well as providing pads to solder the module to the top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
  OLED 128x64 I2C Monochrome Display GND-VDD: OLED 128x64 I2C Monochrome Display. Note: there are two variants of this part, this one is the GND VDD SCK SDA variant. The other is VDD GND SCK SDA. Make sure you select the part that matches your module as using the incorrect part will probably destroy your module! In addition the mounting holes are marked on silkscreen but not by default drilled. If you want drilled mounting holes, copy a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
